// Logisim project calculatorCPU.circ as structural Verilog: 16 circuits, main circuit main
module main (
);

  wire _0_out, _1_out, _2_out, _3_out, _4_out, _5_out, _6_out, _7_out, _8_out, _9_out, button_2_out,
       button_3_out, button_4_out, button_5_out, button_out, C_out, keypad_controller_1_write;
  wire [2:0] lcd_controller_1__7_segment_0_2, lcd_controller_1__7_segment_2_2,
       lcd_controller_1__7_segment_4_2, lcd_controller_1__7_segment_6_2, lcd_controller_1__7_segment_9_2,
       lcd_controller_1_minus_2;
  wire [3:0] lcd_controller_1__7_segment_0, lcd_controller_1__7_segment_2, lcd_controller_1__7_segment_4,
       lcd_controller_1__7_segment_6, lcd_controller_1__7_segment_9, lcd_controller_1_minus;
  wire [6:0] lcd_controller_1__7_segment_1, lcd_controller_1__7_segment_3, lcd_controller_1__7_segment_5,
       lcd_controller_1__7_segment_7, lcd_controller_1__7_segment_8;
  wire [31:0] keypad_controller_1_output, mips_cpu_1_from__t8, mips_cpu_1_from__t9;

  MIPS_CPU mips_cpu_1 (
    .Write_Data_to__t9(keypad_controller_1_output), .Write_Signal_for__t9(keypad_controller_1_write),
    .From__t8(mips_cpu_1_from__t8), .From__t9(mips_cpu_1_from__t9));
  _7_Segment_Display u_7_segment_display_1 (
    .g(lcd_controller_1__7_segment_9[0]), .f(lcd_controller_1__7_segment_9[1]),
    .a(lcd_controller_1__7_segment_9[2]), .b(lcd_controller_1__7_segment_9[3]),
    .e(lcd_controller_1__7_segment_9_2[0]), .d(lcd_controller_1__7_segment_9_2[1]),
    .c(lcd_controller_1__7_segment_9_2[2]));  // open: dp
  _7_Segment_Display u_7_segment_display_2 (
    .g(lcd_controller_1_minus[0]), .f(lcd_controller_1_minus[1]), .a(lcd_controller_1_minus[2]),
    .b(lcd_controller_1_minus[3]), .e(lcd_controller_1_minus_2[0]), .d(lcd_controller_1_minus_2[1]),
    .c(lcd_controller_1_minus_2[2]));  // open: dp
  LCD_Controller lcd_controller_1 (
    .From__t8(mips_cpu_1_from__t8), .Minus({lcd_controller_1_minus_2, lcd_controller_1_minus}),
    ._7_Segment_9({lcd_controller_1__7_segment_9_2, lcd_controller_1__7_segment_9}),
    ._7_Segment_8(lcd_controller_1__7_segment_8), ._7_Segment_7(lcd_controller_1__7_segment_7),
    ._7_Segment_6({lcd_controller_1__7_segment_6_2, lcd_controller_1__7_segment_6}),
    ._7_Segment_5(lcd_controller_1__7_segment_5),
    ._7_Segment_4({lcd_controller_1__7_segment_4_2, lcd_controller_1__7_segment_4}),
    ._7_Segment_3(lcd_controller_1__7_segment_3),
    ._7_Segment_2({lcd_controller_1__7_segment_2_2, lcd_controller_1__7_segment_2}),
    ._7_Segment_1(lcd_controller_1__7_segment_1),
    ._7_Segment_0({lcd_controller_1__7_segment_0_2, lcd_controller_1__7_segment_0}));
  Keypad_Controller keypad_controller_1 (
    .C(C_out), .in_2(button_out), .in_3(button_5_out), .in_4(button_4_out), .in_5(button_3_out),
    .in_6(button_2_out), ._9(_9_out), ._8(_8_out), ._7(_7_out), ._6(_6_out), ._5(_5_out), ._4(_4_out),
    ._3(_3_out), ._2(_2_out), ._1(_1_out), ._0(_0_out), .From__t9(mips_cpu_1_from__t9),
    .Write(keypad_controller_1_write), .Output(keypad_controller_1_output));
  _7_Segment_Display u_7_segment_display_3 (
    .g(lcd_controller_1__7_segment_7[0]), .f(lcd_controller_1__7_segment_7[1]),
    .a(lcd_controller_1__7_segment_7[2]), .b(lcd_controller_1__7_segment_7[3]),
    .e(lcd_controller_1__7_segment_7[4]), .d(lcd_controller_1__7_segment_7[5]),
    .c(lcd_controller_1__7_segment_7[6]));  // open: dp
  _7_Segment_Display u_7_segment_display_4 (
    .g(lcd_controller_1__7_segment_8[0]), .f(lcd_controller_1__7_segment_8[1]),
    .a(lcd_controller_1__7_segment_8[2]), .b(lcd_controller_1__7_segment_8[3]),
    .e(lcd_controller_1__7_segment_8[4]), .d(lcd_controller_1__7_segment_8[5]),
    .c(lcd_controller_1__7_segment_8[6]));  // open: dp
  _7_Segment_Display u_7_segment_display_5 (
    .g(lcd_controller_1__7_segment_5[0]), .f(lcd_controller_1__7_segment_5[1]),
    .a(lcd_controller_1__7_segment_5[2]), .b(lcd_controller_1__7_segment_5[3]),
    .e(lcd_controller_1__7_segment_5[4]), .d(lcd_controller_1__7_segment_5[5]),
    .c(lcd_controller_1__7_segment_5[6]));  // open: dp
  _7_Segment_Display u_7_segment_display_6 (
    .g(lcd_controller_1__7_segment_6[0]), .f(lcd_controller_1__7_segment_6[1]),
    .a(lcd_controller_1__7_segment_6[2]), .b(lcd_controller_1__7_segment_6[3]),
    .e(lcd_controller_1__7_segment_6_2[0]), .d(lcd_controller_1__7_segment_6_2[1]),
    .c(lcd_controller_1__7_segment_6_2[2]));  // open: dp
  Button _7 (.out(_7_out));
  Button _4 (.out(_4_out));
  Button _1 (.out(_1_out));
  Button _0 (.out(_0_out));
  Instruction_Memory__DONE instruction_memory_done_1 ();  // open: Address, out_2
  _7_Segment_Display u_7_segment_display_7 (
    .g(lcd_controller_1__7_segment_3[0]), .f(lcd_controller_1__7_segment_3[1]),
    .a(lcd_controller_1__7_segment_3[2]), .b(lcd_controller_1__7_segment_3[3]),
    .e(lcd_controller_1__7_segment_3[4]), .d(lcd_controller_1__7_segment_3[5]),
    .c(lcd_controller_1__7_segment_3[6]));  // open: dp
  _7_Segment_Display u_7_segment_display_8 (
    .g(lcd_controller_1__7_segment_4[0]), .f(lcd_controller_1__7_segment_4[1]),
    .a(lcd_controller_1__7_segment_4[2]), .b(lcd_controller_1__7_segment_4[3]),
    .e(lcd_controller_1__7_segment_4_2[0]), .d(lcd_controller_1__7_segment_4_2[1]),
    .c(lcd_controller_1__7_segment_4_2[2]));  // open: dp
  Button _8 (.out(_8_out));
  Button _5 (.out(_5_out));
  Button _2 (.out(_2_out));
  Button C (.out(C_out));
  _7_Segment_Display u_7_segment_display_9 (
    .g(lcd_controller_1__7_segment_2[0]), .f(lcd_controller_1__7_segment_2[1]),
    .a(lcd_controller_1__7_segment_2[2]), .b(lcd_controller_1__7_segment_2[3]),
    .e(lcd_controller_1__7_segment_2_2[0]), .d(lcd_controller_1__7_segment_2_2[1]),
    .c(lcd_controller_1__7_segment_2_2[2]));  // open: dp
  _7_Segment_Display u_7_segment_display_10 (
    .g(lcd_controller_1__7_segment_1[0]), .f(lcd_controller_1__7_segment_1[1]),
    .a(lcd_controller_1__7_segment_1[2]), .b(lcd_controller_1__7_segment_1[3]),
    .e(lcd_controller_1__7_segment_1[4]), .d(lcd_controller_1__7_segment_1[5]),
    .c(lcd_controller_1__7_segment_1[6]));  // open: dp
  Button _9 (.out(_9_out));
  Button _6 (.out(_6_out));
  Button _3 (.out(_3_out));
  Button button (.out(button_out));
  _7_Segment_Display u_7_segment_display_11 (
    .g(lcd_controller_1__7_segment_0[0]), .f(lcd_controller_1__7_segment_0[1]),
    .a(lcd_controller_1__7_segment_0[2]), .b(lcd_controller_1__7_segment_0[3]),
    .e(lcd_controller_1__7_segment_0_2[0]), .d(lcd_controller_1__7_segment_0_2[1]),
    .c(lcd_controller_1__7_segment_0_2[2]));  // open: dp
  Button button_2 (.out(button_2_out));
  Button button_3 (.out(button_3_out));
  Button button_4 (.out(button_4_out));
  Button button_5 (.out(button_5_out));

  // Notes on the sheet:
  //   From $t8
  //   From $t9
  //   Write Data to $t9
  //   Write Signal for $t9
endmodule

module LCD_Controller (
  input  [31:0] From__t8,
  output [6:0] Minus,
  output [6:0] _7_Segment_9,
  output [6:0] _7_Segment_8,
  output [6:0] _7_Segment_7,
  output [6:0] _7_Segment_6,
  output [6:0] _7_Segment_5,
  output [6:0] _7_Segment_4,
  output [6:0] _7_Segment_3,
  output [6:0] _7_Segment_2,
  output [6:0] _7_Segment_1,
  output [6:0] _7_Segment_0
);

  wire [3:0] binarytobcd_1_bcd0, binarytobcd_1_bcd1, binarytobcd_1_bcd2, binarytobcd_1_bcd3,
       binarytobcd_1_bcd4, binarytobcd_1_bcd5, binarytobcd_1_bcd6, binarytobcd_1_bcd7, binarytobcd_1_bcd8,
       binarytobcd_1_bcd9;

  BinaryToBCD binarytobcd_1 (
    .Input(From__t8), .Minus(Minus[0]), .BCD9(binarytobcd_1_bcd9), .BCD8(binarytobcd_1_bcd8),
    .BCD7(binarytobcd_1_bcd7), .BCD6(binarytobcd_1_bcd6), .BCD5(binarytobcd_1_bcd5),
    .BCD4(binarytobcd_1_bcd4), .BCD3(binarytobcd_1_bcd3), .BCD2(binarytobcd_1_bcd2),
    .BCD1(binarytobcd_1_bcd1), .BCD0(binarytobcd_1_bcd0));
  _7_Segment_Controller u_7_segment_controller_1 (.BCD(binarytobcd_1_bcd9), .out_2(_7_Segment_9));
  _7_Segment_Controller u_7_segment_controller_2 (.BCD(binarytobcd_1_bcd8), .out_2(_7_Segment_8));
  _7_Segment_Controller u_7_segment_controller_3 (.BCD(binarytobcd_1_bcd7), .out_2(_7_Segment_7));
  _7_Segment_Controller u_7_segment_controller_4 (.BCD(binarytobcd_1_bcd6), .out_2(_7_Segment_6));
  _7_Segment_Controller u_7_segment_controller_5 (.BCD(binarytobcd_1_bcd5), .out_2(_7_Segment_5));
  _7_Segment_Controller u_7_segment_controller_6 (.BCD(binarytobcd_1_bcd4), .out_2(_7_Segment_4));
  _7_Segment_Controller u_7_segment_controller_7 (.BCD(binarytobcd_1_bcd3), .out_2(_7_Segment_3));
  _7_Segment_Controller u_7_segment_controller_8 (.BCD(binarytobcd_1_bcd2), .out_2(_7_Segment_2));
  _7_Segment_Controller u_7_segment_controller_9 (.BCD(binarytobcd_1_bcd1), .out_2(_7_Segment_1));
  _7_Segment_Controller u_7_segment_controller_10 (.BCD(binarytobcd_1_bcd0), .out_2(_7_Segment_0));

  assign Minus[6:1] = {6{1'b0}};
endmodule

module _7_Segment_Controller (
  input  [3:0] BCD,
  output [6:0] out_2
);

  wire and_1_out, and_2_out, and_3_out, and_4_out, and_5_out, and_6_out, and_7_out, and_8_out, and_9_out,
       and_10_out, and_11_out, and_12_out, and_13_out, and_14_out, and_15_out, and_16_out, not_1_out,
       not_2_out, not_3_out, not_4_out, not_5_out, not_6_out, not_7_out, not_8_out, not_9_out, not_10_out,
       not_11_out, not_12_out, not_13_out, not_14_out, not_15_out, not_16_out, not_17_out, not_18_out,
       not_19_out, not_20_out, not_21_out;

  not not_1 (not_1_out, BCD[2]);
  not not_2 (not_2_out, BCD[0]);
  not not_3 (not_3_out, BCD[1]);
  not not_4 (not_4_out, BCD[1]);
  not not_5 (not_5_out, BCD[0]);
  not not_6 (not_6_out, BCD[1]);
  not not_7 (not_7_out, BCD[0]);
  not not_8 (not_8_out, BCD[2]);
  not not_9 (not_9_out, BCD[0]);
  not not_10 (not_10_out, BCD[1]);
  not not_11 (not_11_out, BCD[0]);
  not not_12 (not_12_out, BCD[2]);
  not not_13 (not_13_out, BCD[0]);
  not not_14 (not_14_out, BCD[0]);
  not not_15 (not_15_out, BCD[2]);
  not not_16 (not_16_out, BCD[0]);
  not not_17 (not_17_out, BCD[2]);
  not not_18 (not_18_out, BCD[0]);
  not not_19 (not_19_out, BCD[1]);
  not not_20 (not_20_out, BCD[1]);
  and and_1 (and_1_out, not_1_out, BCD[1]);
  and and_2 (and_2_out, BCD[1], not_2_out);
  and and_3 (and_3_out, BCD[2], not_3_out);
  and and_4 (and_4_out, not_4_out, not_5_out);
  and and_5 (and_5_out, BCD[2], not_6_out);
  and and_6 (and_6_out, BCD[2], not_7_out);
  and and_7 (and_7_out, not_8_out, not_9_out);
  and and_8 (and_8_out, BCD[2], BCD[0]);
  not not_21 (not_21_out, BCD[2]);
  and and_9 (and_9_out, not_10_out, not_11_out);
  and and_10 (and_10_out, BCD[1], BCD[0]);
  and and_11 (and_11_out, not_12_out, not_13_out);
  and and_12 (and_12_out, BCD[1], not_14_out);
  and and_13 (and_13_out, not_15_out, not_16_out);
  and and_14 (and_14_out, not_17_out, BCD[1]);
  and and_15 (and_15_out, BCD[1], not_18_out);
  and and_16 (and_16_out, BCD[2], not_19_out, BCD[0]);
  or or_1 (out_2[6], not_20_out, BCD[0], BCD[2]);
  or or_2 (out_2[0], and_1_out, and_2_out, and_3_out, BCD[3]);
  or or_3 (out_2[1], and_4_out, and_5_out, and_6_out, BCD[3]);
  or or_4 (out_2[2], and_7_out, BCD[1], and_8_out, BCD[3]);
  or or_5 (out_2[3], not_21_out, and_9_out, and_10_out);
  or or_6 (out_2[4], and_11_out, and_12_out);
  or or_7 (out_2[5], and_13_out, and_14_out, and_15_out, and_16_out);
endmodule

module BinaryToBCD (
  input  [31:0] Input,
  output Minus,
  output [3:0] BCD9,
  output [3:0] BCD8,
  output [3:0] BCD7,
  output [3:0] BCD6,
  output [3:0] BCD5,
  output [3:0] BCD4,
  output [3:0] BCD3,
  output [3:0] BCD2,
  output [3:0] BCD1,
  output [3:0] BCD0
);

  wire [27:0] subtractor_1_out, subtractor_2_out, subtractor_3_out, subtractor_4_out, subtractor_5_out,
       subtractor_6_out, subtractor_7_out, subtractor_8_out, subtractor_9_out;
  wire [31:0] adder_1_out, divider_1_out, divider_2_out, divider_3_out, divider_4_out, divider_5_out,
       divider_6_out, divider_7_out, divider_8_out, multiplexer_1_out, multiplier_1_out, multiplier_2_out,
       multiplier_3_out, multiplier_4_out, multiplier_5_out, multiplier_6_out, multiplier_7_out,
       multiplier_8_out, multiplier_9_out, not_1_out;
  wire [31:4] divider_9_out;

  assign not_1_out = ~Input;  // NOT_Gate not_1, 32 bits wide
  Adder #(.width(32)) adder_1 (.a(not_1_out), .b(32'h1), .out(adder_1_out));  // open: cin, cout
  Multiplexer #(.width(32)) multiplexer_1 (
    .in0(Input), .in1(adder_1_out), .out(multiplexer_1_out), .sel(Input[31]));  // open: en
  Subtractor #(.width(32)) subtractor_1 (
    .a(multiplexer_1_out), .b(multiplier_1_out), .out({subtractor_1_out, BCD0}));  // open: bin, bout
  Multiplier #(.width(32)) multiplier_1 (.a(divider_1_out), .b(32'ha), .out(multiplier_1_out));  // open: cin, cout
  Divider #(.width(32)) divider_1 (.a(multiplexer_1_out), .b(32'ha), .out(divider_1_out));  // open: upper, rem
  Subtractor #(.width(32)) subtractor_2 (
    .a(divider_1_out), .b(multiplier_2_out), .out({subtractor_2_out, BCD1}));  // open: bin, bout
  Multiplier #(.width(32)) multiplier_2 (.a(divider_2_out), .b(32'ha), .out(multiplier_2_out));  // open: cin, cout
  Divider #(.width(32)) divider_2 (.a(divider_1_out), .b(32'ha), .out(divider_2_out));  // open: upper, rem
  Subtractor #(.width(32)) subtractor_3 (
    .a(divider_2_out), .b(multiplier_3_out), .out({subtractor_3_out, BCD2}));  // open: bin, bout
  Multiplier #(.width(32)) multiplier_3 (.a(divider_3_out), .b(32'ha), .out(multiplier_3_out));  // open: cin, cout
  Divider #(.width(32)) divider_3 (.a(divider_2_out), .b(32'ha), .out(divider_3_out));  // open: upper, rem
  Subtractor #(.width(32)) subtractor_4 (
    .a(divider_3_out), .b(multiplier_4_out), .out({subtractor_4_out, BCD3}));  // open: bin, bout
  Multiplier #(.width(32)) multiplier_4 (.a(divider_4_out), .b(32'ha), .out(multiplier_4_out));  // open: cin, cout
  Divider #(.width(32)) divider_4 (.a(divider_3_out), .b(32'ha), .out(divider_4_out));  // open: upper, rem
  Subtractor #(.width(32)) subtractor_5 (
    .a(divider_4_out), .b(multiplier_5_out), .out({subtractor_5_out, BCD4}));  // open: bin, bout
  Multiplier #(.width(32)) multiplier_5 (.a(divider_5_out), .b(32'ha), .out(multiplier_5_out));  // open: cin, cout
  Divider #(.width(32)) divider_5 (.a(divider_4_out), .b(32'ha), .out(divider_5_out));  // open: upper, rem
  Subtractor #(.width(32)) subtractor_6 (
    .a(divider_5_out), .b(multiplier_6_out), .out({subtractor_6_out, BCD5}));  // open: bin, bout
  Multiplier #(.width(32)) multiplier_6 (.a(divider_6_out), .b(32'ha), .out(multiplier_6_out));  // open: cin, cout
  Divider #(.width(32)) divider_6 (.a(divider_5_out), .b(32'ha), .out(divider_6_out));  // open: upper, rem
  Subtractor #(.width(32)) subtractor_7 (
    .a(divider_6_out), .b(multiplier_7_out), .out({subtractor_7_out, BCD6}));  // open: bin, bout
  Multiplier #(.width(32)) multiplier_7 (.a(divider_7_out), .b(32'ha), .out(multiplier_7_out));  // open: cin, cout
  Divider #(.width(32)) divider_7 (.a(divider_6_out), .b(32'ha), .out(divider_7_out));  // open: upper, rem
  Subtractor #(.width(32)) subtractor_8 (
    .a(divider_7_out), .b(multiplier_8_out), .out({subtractor_8_out, BCD7}));  // open: bin, bout
  Multiplier #(.width(32)) multiplier_8 (.a(divider_8_out), .b(32'ha), .out(multiplier_8_out));  // open: cin, cout
  Divider #(.width(32)) divider_8 (.a(divider_7_out), .b(32'ha), .out(divider_8_out));  // open: upper, rem
  Subtractor #(.width(32)) subtractor_9 (
    .a(divider_8_out), .b(multiplier_9_out), .out({subtractor_9_out, BCD8}));  // open: bin, bout
  Multiplier #(.width(32)) multiplier_9 (
    .a({divider_9_out, BCD9}), .b(32'ha), .out(multiplier_9_out));  // open: cin, cout
  Divider #(.width(32)) divider_9 (.a(divider_8_out), .b(32'ha), .out({divider_9_out, BCD9}));  // open: upper, rem

  assign Minus = Input[31];
endmodule

module Keypad_Controller (
  input  C,
  input  in_2,
  input  in_3,
  input  in_4,
  input  in_5,
  input  in_6,
  input  _9,
  input  _8,
  input  _7,
  input  _6,
  input  _5,
  input  _4,
  input  _3,
  input  _2,
  input  _1,
  input  _0,
  input  [31:0] From__t9,
  output Write,
  output [31:0] Output
);

  wire iszero_1_out_2, iszero_2_out_2;
  wire [3:0] or_4_out;
  wire [15:0] and_1_out;

  and and_1 (and_1_out[0], C, iszero_1_out_2);
  and and_2 (and_1_out[1], in_2, iszero_1_out_2);
  and and_3 (and_1_out[2], in_3, iszero_1_out_2);
  and and_4 (and_1_out[3], in_4, iszero_1_out_2);
  and and_5 (and_1_out[4], in_5, iszero_1_out_2);
  and and_6 (and_1_out[5], in_6, iszero_1_out_2);
  and and_7 (and_1_out[6], _9, iszero_1_out_2);
  and and_8 (and_1_out[7], _8, iszero_1_out_2);
  and and_9 (and_1_out[8], _7, iszero_1_out_2);
  and and_10 (and_1_out[9], _6, iszero_1_out_2);
  and and_11 (and_1_out[10], _5, iszero_1_out_2);
  and and_12 (and_1_out[11], _4, iszero_1_out_2);
  and and_13 (and_1_out[12], _3, iszero_1_out_2);
  and and_14 (and_1_out[13], _2, iszero_1_out_2);
  and and_15 (and_1_out[14], _1, iszero_1_out_2);
  and and_16 (and_1_out[15], _0, iszero_1_out_2);
  isZero iszero_1 (.Input(From__t9), .out_2(iszero_1_out_2));
  or or_1 (or_4_out[3], and_1_out[0], and_1_out[1], and_1_out[2], and_1_out[3], and_1_out[4], and_1_out[5], and_1_out[6], and_1_out[7]);
  or or_2 (or_4_out[2], and_1_out[8], and_1_out[9], and_1_out[10], and_1_out[11], and_1_out[0], and_1_out[1], and_1_out[2], and_1_out[3]);
  or or_3 (or_4_out[1], and_1_out[12], and_1_out[13], and_1_out[9], and_1_out[8], and_1_out[5], and_1_out[4], and_1_out[1], and_1_out[0]);
  or or_4 (or_4_out[0], and_1_out[12], and_1_out[14], and_1_out[10], and_1_out[8], and_1_out[6], and_1_out[4], and_1_out[2], and_1_out[0]);
  isZero iszero_2 (.Input({{16{1'b0}}, and_1_out}), .out_2(iszero_2_out_2));
  not not_1 (Write, iszero_2_out_2);
  assign Output = Write ? {28'h8000000, or_4_out} : 32'bz;  // Controlled_Buffer controlled_buffer_1
endmodule

module isZero (
  input  [31:0] Input,
  output out_2
);

  wire or_1_out;

  not not_1 (out_2, or_1_out);
  or or_1 (or_1_out, Input[0], Input[1], Input[2], Input[3], Input[4], Input[5], Input[6], Input[7], Input[8], Input[9], Input[10], Input[11], Input[12], Input[13], Input[14], Input[15], Input[16], Input[17], Input[18], Input[19], Input[20], Input[21], Input[22], Input[23], Input[24], Input[25], Input[26], Input[27], Input[28], Input[29], Input[30], Input[31]);
endmodule

module Instruction_Memory__DONE (
  input  [15:0] Address,
  output [31:0] out_2
);

  ROM #(.addrWidth(16), .dataWidth(32)) rom_1 (.addr(Address), .data(out_2), .sel(1'b1));

  // Notes on the sheet:
  //   contents of rom_1 (hex, n*v repeats v):
  //   c820 196020 c020 5020 a020 200e000a 8020 8820 9020 9820 810000b 1320ffff 332c000f 2001000e 102c0029
  //   2001000f 102c002c 18e682a 20010001 142d001f 20010001 102d000b 1320ffff 332c000f 2001000e 102c001e
  //   2001000f 102c0021 18e682a 20010001 142d0014 20010001 102d0009 105820 1080c0 20b8020 20b8020 20c8020
  //   6020 c820 10c020 810000b 115820 1188c0 22b8820 22b8820 22c8820 6020 c820 11c020 810003e c9020 10c020
  //   6020 c820 8100016 109820 13c020 6020 c820 81000c1 8100000 1320ffff 332c000f 2001000e 102c0007
  //   2001000f 102cfff9 18e682a 20010001 142d003a 20010001 102dffe1 2001000a 10320006 2001000b 1032000a
  //   2001000c 1032000e 2001000d 1032001c 2119820 13c020 8820 6020 c820 81000c1 2119822 13c020 8820 6020
  //   c820 81000c1 2005020 2204820 8100060 11200003 10a4020 2129ffff 8100060 1009820 13c020 5020 4820 4020
  //   8820 6020 c820 81000c1 2005020 2204820 a020 8100071 141a82a 2aa10001 14200003 1495022 22940001
  //   8100071 2809820 13c020 a020 4820 5020 a820 8820 6020 c820 81000c1 2001000a 10320006 2001000b
  //   1032000c 2001000c 10320012 2001000d 10320022 2119820 13c020 138020 c9020 8820 6020 c820 8100016
  //   2119822 13c020 138020 c9020 8820 6020 c820 8100016 2005020 2204820 810009c 11200003 10a4020 2129ffff
  //   810009c 1009820 13c020 138020 c9020 5020 4820 4020 8820 6020 c820 8100016 2005020 2204820 a020
  //   81000af 141a82a 2aa10001 14200003 1495022 22940001 81000af 2809820 13c020 138020 c9020 a020 4820
  //   5020 a820 8820 6020 c820 8100016 1320ffff 332c000f 2001000e 102c0007 2001000f 102cff76 18e682a
  //   20010001 142d0008 20010001 102d000d 13c020 8820 8820 6020 c820 81000c1 138020 c9020 8820 8820 6020
  //   c820 8100016 c8020 10c020 6020 c820 810000b
endmodule

module Shift_Left__DONE (
  input  [31:0] Input,
  input  [4:0] Shamt,
  output [31:0] out_3
);

  Shifter #(.width(32)) shifter_1 (.in(Input), .\dist (Shamt), .out(out_3));
endmodule

module Shift_Right__DONE (
  input  [31:0] Input,
  input  [4:0] Shamt,
  output [31:0] out_3
);

  Shifter #(.width(32), .shift("lr")) shifter_1 (.in(Input), .\dist (Shamt), .out(out_3));
endmodule

module Sign_Extend__DONE (
  input  [15:0] Input,
  output [31:0] Output
);


  assign Output = {{17{Input[15]}}, Input[14:0]};
endmodule

module Register_File__DONE (
  input  [4:0] Read_Register_1,
  input  RegWrite,
  input  Write_Enable,
  input  [4:0] Write_Register,
  input  [31:0] Write_Data,
  input  [4:0] Read_Register_2,
  input  [31:0] Write_to__t9,
  input  Write_Signal,
  input  Clock,
  output [31:0] Read_Data_1,
  output [31:0] Read_Data_2,
  output [31:0] t8_to_LCD,
  output [31:0] t9_to_Keypad
);

  wire and_1_out, and_2_out, and_3_out, and_4_out, and_5_out, and_6_out, and_7_out, and_8_out, and_9_out,
       and_10_out, and_11_out, and_12_out, and_13_out, and_14_out, and_15_out, and_16_out, and_17_out,
       and_18_out, and_19_out, and_20_out, and_21_out, and_22_out, and_23_out, and_24_out, and_25_out,
       and_26_out, and_27_out, and_28_out, and_29_out, and_30_out, and_31_out, and_32_out,
       controlled_buffer_1_out, demultiplexer_1_out0, demultiplexer_1_out1, demultiplexer_1_out2,
       demultiplexer_1_out3, demultiplexer_1_out4, demultiplexer_1_out5, demultiplexer_1_out6,
       demultiplexer_1_out7, demultiplexer_1_out8, demultiplexer_1_out9, demultiplexer_1_out10,
       demultiplexer_1_out11, demultiplexer_1_out12, demultiplexer_1_out13, demultiplexer_1_out14,
       demultiplexer_1_out15, demultiplexer_1_out16, demultiplexer_1_out17, demultiplexer_1_out18,
       demultiplexer_1_out19, demultiplexer_1_out20, demultiplexer_1_out21, demultiplexer_1_out22,
       demultiplexer_1_out23, demultiplexer_1_out24, demultiplexer_1_out25, demultiplexer_1_out26,
       demultiplexer_1_out27, demultiplexer_1_out28, demultiplexer_1_out29, demultiplexer_1_out30,
       demultiplexer_1_out31;
  wire [31:0] controlled_buffer_2_out, Reg_0_q, Reg_1_q, Reg_2_q, Reg_3_q, Reg_4_q, Reg_5_q, Reg_6_q,
       Reg_7_q, Reg_8_q, Reg_9_q, Reg_10_q, Reg_11_q, Reg_12_q, Reg_13_q, Reg_14_q, Reg_15_q, Reg_16_q,
       Reg_17_q, Reg_18_q, Reg_19_q, Reg_20_q, Reg_21_q, Reg_22_q, Reg_23_q, Reg_26_q, Reg_27_q, Reg_28_q,
       Reg_29_q, Reg_30_q, Reg_31_q;

  assign controlled_buffer_1_out = Write_Signal ? Write_Signal : 1'bz;  // Controlled_Buffer controlled_buffer_1
  assign controlled_buffer_2_out = Write_Signal ? Write_to__t9 : 32'bz;  // Controlled_Buffer controlled_buffer_2
  assign controlled_buffer_2_out = and_26_out ? Write_Data : 32'bz;  // Controlled_Buffer controlled_buffer_3
  assign controlled_buffer_1_out = and_26_out ? and_26_out : 1'bz;  // Controlled_Buffer controlled_buffer_4
  Demultiplexer #(.select(5)) demultiplexer_1 (
    .out0(demultiplexer_1_out0), .out1(demultiplexer_1_out1), .out2(demultiplexer_1_out2),
    .out3(demultiplexer_1_out3), .out4(demultiplexer_1_out4), .out5(demultiplexer_1_out5),
    .out6(demultiplexer_1_out6), .out7(demultiplexer_1_out7), .out8(demultiplexer_1_out8),
    .out9(demultiplexer_1_out9), .out10(demultiplexer_1_out10), .out11(demultiplexer_1_out11),
    .out12(demultiplexer_1_out12), .out13(demultiplexer_1_out13), .out14(demultiplexer_1_out14),
    .out15(demultiplexer_1_out15), .out16(demultiplexer_1_out16), .out17(demultiplexer_1_out17),
    .out18(demultiplexer_1_out18), .out19(demultiplexer_1_out19), .out20(demultiplexer_1_out20),
    .out21(demultiplexer_1_out21), .out22(demultiplexer_1_out22), .out23(demultiplexer_1_out23),
    .out24(demultiplexer_1_out24), .out25(demultiplexer_1_out25), .out26(demultiplexer_1_out26),
    .out27(demultiplexer_1_out27), .out28(demultiplexer_1_out28), .out29(demultiplexer_1_out29),
    .out30(demultiplexer_1_out30), .out31(demultiplexer_1_out31), .in(Write_Enable), .sel(Write_Register));  // open: en
  and and_1 (and_1_out, demultiplexer_1_out0, RegWrite);
  and and_2 (and_2_out, demultiplexer_1_out1, RegWrite);
  and and_3 (and_3_out, demultiplexer_1_out2, RegWrite);
  and and_4 (and_4_out, demultiplexer_1_out3, RegWrite);
  and and_5 (and_5_out, demultiplexer_1_out4, RegWrite);
  and and_6 (and_6_out, demultiplexer_1_out5, RegWrite);
  and and_7 (and_7_out, demultiplexer_1_out6, RegWrite);
  and and_8 (and_8_out, demultiplexer_1_out7, RegWrite);
  and and_9 (and_9_out, demultiplexer_1_out8, RegWrite);
  and and_10 (and_10_out, demultiplexer_1_out9, RegWrite);
  and and_11 (and_11_out, demultiplexer_1_out10, RegWrite);
  and and_12 (and_12_out, demultiplexer_1_out11, RegWrite);
  and and_13 (and_13_out, demultiplexer_1_out12, RegWrite);
  and and_14 (and_14_out, demultiplexer_1_out13, RegWrite);
  and and_15 (and_15_out, demultiplexer_1_out14, RegWrite);
  and and_16 (and_16_out, demultiplexer_1_out15, RegWrite);
  and and_17 (and_17_out, demultiplexer_1_out16, RegWrite);
  and and_18 (and_18_out, demultiplexer_1_out17, RegWrite);
  and and_19 (and_19_out, demultiplexer_1_out18, RegWrite);
  and and_20 (and_20_out, demultiplexer_1_out19, RegWrite);
  and and_21 (and_21_out, demultiplexer_1_out20, RegWrite);
  and and_22 (and_22_out, demultiplexer_1_out21, RegWrite);
  and and_23 (and_23_out, demultiplexer_1_out22, RegWrite);
  and and_24 (and_24_out, demultiplexer_1_out23, RegWrite);
  and and_25 (and_25_out, demultiplexer_1_out24, RegWrite);
  and and_26 (and_26_out, demultiplexer_1_out25, RegWrite);
  and and_27 (and_27_out, demultiplexer_1_out26, RegWrite);
  and and_28 (and_28_out, demultiplexer_1_out27, RegWrite);
  and and_29 (and_29_out, demultiplexer_1_out28, RegWrite);
  and and_30 (and_30_out, demultiplexer_1_out29, RegWrite);
  and and_31 (and_31_out, demultiplexer_1_out30, RegWrite);
  and and_32 (and_32_out, demultiplexer_1_out31, RegWrite);
  Register #(.width(32)) Reg_0 (.D(Write_Data), .en(and_1_out), .Q(Reg_0_q), .clk(Clock));  // open: clr
  Register #(.width(32)) Reg_1 (.D(Write_Data), .en(and_2_out), .Q(Reg_1_q), .clk(Clock));  // open: clr
  Register #(.width(32)) Reg_2 (.D(Write_Data), .en(and_3_out), .Q(Reg_2_q), .clk(Clock));  // open: clr
  Register #(.width(32)) Reg_3 (.D(Write_Data), .en(and_4_out), .Q(Reg_3_q), .clk(Clock));  // open: clr
  Register #(.width(32)) Reg_4 (.D(Write_Data), .en(and_5_out), .Q(Reg_4_q), .clk(Clock));  // open: clr
  Register #(.width(32)) Reg_5 (.D(Write_Data), .en(and_6_out), .Q(Reg_5_q), .clk(Clock));  // open: clr
  Register #(.width(32)) Reg_6 (.D(Write_Data), .en(and_7_out), .Q(Reg_6_q), .clk(Clock));  // open: clr
  Register #(.width(32)) Reg_7 (.D(Write_Data), .en(and_8_out), .Q(Reg_7_q), .clk(Clock));  // open: clr
  Register #(.width(32)) Reg_8 (.D(Write_Data), .en(and_9_out), .Q(Reg_8_q), .clk(Clock));  // open: clr
  Register #(.width(32)) Reg_9 (.D(Write_Data), .en(and_10_out), .Q(Reg_9_q), .clk(Clock));  // open: clr
  Register #(.width(32)) Reg_10 (.D(Write_Data), .en(and_11_out), .Q(Reg_10_q), .clk(Clock));  // open: clr
  Register #(.width(32)) Reg_11 (.D(Write_Data), .en(and_12_out), .Q(Reg_11_q), .clk(Clock));  // open: clr
  Register #(.width(32)) Reg_12 (.D(Write_Data), .en(and_13_out), .Q(Reg_12_q), .clk(Clock));  // open: clr
  Register #(.width(32)) Reg_13 (.D(Write_Data), .en(and_14_out), .Q(Reg_13_q), .clk(Clock));  // open: clr
  Register #(.width(32)) Reg_14 (.D(Write_Data), .en(and_15_out), .Q(Reg_14_q), .clk(Clock));  // open: clr
  Register #(.width(32)) Reg_15 (.D(Write_Data), .en(and_16_out), .Q(Reg_15_q), .clk(Clock));  // open: clr
  Register #(.width(32)) Reg_16 (.D(Write_Data), .en(and_17_out), .Q(Reg_16_q), .clk(Clock));  // open: clr
  Register #(.width(32)) Reg_17 (.D(Write_Data), .en(and_18_out), .Q(Reg_17_q), .clk(Clock));  // open: clr
  Register #(.width(32)) Reg_18 (.D(Write_Data), .en(and_19_out), .Q(Reg_18_q), .clk(Clock));  // open: clr
  Register #(.width(32)) Reg_19 (.D(Write_Data), .en(and_20_out), .Q(Reg_19_q), .clk(Clock));  // open: clr
  Register #(.width(32)) Reg_20 (.D(Write_Data), .en(and_21_out), .Q(Reg_20_q), .clk(Clock));  // open: clr
  Register #(.width(32)) Reg_21 (.D(Write_Data), .en(and_22_out), .Q(Reg_21_q), .clk(Clock));  // open: clr
  Register #(.width(32)) Reg_22 (.D(Write_Data), .en(and_23_out), .Q(Reg_22_q), .clk(Clock));  // open: clr
  Register #(.width(32)) Reg_23 (.D(Write_Data), .en(and_24_out), .Q(Reg_23_q), .clk(Clock));  // open: clr
  Register #(.width(32)) Reg_24 (.D(Write_Data), .en(and_25_out), .Q(t8_to_LCD), .clk(Clock));  // open: clr
  Register #(.width(32)) Reg_25 (
    .D(controlled_buffer_2_out), .en(controlled_buffer_1_out), .Q(t9_to_Keypad), .clk(Clock));  // open: clr
  Register #(.width(32)) Reg_26 (.D(Write_Data), .en(and_27_out), .Q(Reg_26_q), .clk(Clock));  // open: clr
  Register #(.width(32)) Reg_27 (.D(Write_Data), .en(and_28_out), .Q(Reg_27_q), .clk(Clock));  // open: clr
  Register #(.width(32)) Reg_28 (.D(Write_Data), .en(and_29_out), .Q(Reg_28_q), .clk(Clock));  // open: clr
  Register #(.width(32)) Reg_29 (.D(Write_Data), .en(and_30_out), .Q(Reg_29_q), .clk(Clock));  // open: clr
  Register #(.width(32)) Reg_30 (.D(Write_Data), .en(and_31_out), .Q(Reg_30_q), .clk(Clock));  // open: clr
  Register #(.width(32)) Reg_31 (.D(Write_Data), .en(and_32_out), .Q(Reg_31_q), .clk(Clock));  // open: clr
  Multiplexer #(.select(5), .width(32)) multiplexer_1 (
    .in0(Reg_0_q), .in1(Reg_1_q), .in2(Reg_2_q), .in3(Reg_3_q), .in4(Reg_4_q), .in5(Reg_5_q), .in6(Reg_6_q),
    .in7(Reg_7_q), .in8(Reg_8_q), .in9(Reg_9_q), .in10(Reg_10_q), .in11(Reg_11_q), .in12(Reg_12_q),
    .in13(Reg_13_q), .in14(Reg_14_q), .in15(Reg_15_q), .in16(Reg_16_q), .in17(Reg_17_q), .in18(Reg_18_q),
    .in19(Reg_19_q), .in20(Reg_20_q), .in21(Reg_21_q), .in22(Reg_22_q), .in23(Reg_23_q), .in24(t8_to_LCD),
    .in25(t9_to_Keypad), .in26(Reg_26_q), .in27(Reg_27_q), .in28(Reg_28_q), .in29(Reg_29_q), .in30(Reg_30_q),
    .in31(Reg_31_q), .out(Read_Data_1), .sel(Read_Register_1));  // open: en
  Multiplexer #(.select(5), .width(32)) multiplexer_2 (
    .in0(Reg_0_q), .in1(Reg_1_q), .in2(Reg_2_q), .in3(Reg_3_q), .in4(Reg_4_q), .in5(Reg_5_q), .in6(Reg_6_q),
    .in7(Reg_7_q), .in8(Reg_8_q), .in9(Reg_9_q), .in10(Reg_10_q), .in11(Reg_11_q), .in12(Reg_12_q),
    .in13(Reg_13_q), .in14(Reg_14_q), .in15(Reg_15_q), .in16(Reg_16_q), .in17(Reg_17_q), .in18(Reg_18_q),
    .in19(Reg_19_q), .in20(Reg_20_q), .in21(Reg_21_q), .in22(Reg_22_q), .in23(Reg_23_q), .in24(t8_to_LCD),
    .in25(t9_to_Keypad), .in26(Reg_26_q), .in27(Reg_27_q), .in28(Reg_28_q), .in29(Reg_29_q), .in30(Reg_30_q),
    .in31(Reg_31_q), .out(Read_Data_2), .sel(Read_Register_2));  // open: en
endmodule

module Control_Unit__DONE (
  input  [5:0] Opcode,
  output Jump,
  output beq,
  output bne,
  output RegWrite,
  output RegDst,
  output [1:0] ALUOp
);

  wire and_6_out, not_1_out, not_2_out, not_3_out, not_4_out, not_5_out, not_6_out, not_7_out, not_8_out,
       not_9_out, not_10_out, not_11_out, not_12_out, not_13_out, not_14_out, not_15_out, not_16_out,
       not_17_out, not_18_out, not_19_out, not_20_out, not_21_out, not_22_out, or_1_out;

  not not_1 (not_1_out, Opcode[5]);
  not not_2 (not_2_out, Opcode[3]);
  and and_1 (RegDst, not_2_out, not_1_out);
  not not_3 (not_3_out, Opcode[3]);
  not not_4 (not_4_out, Opcode[5]);
  not not_5 (not_5_out, Opcode[1]);
  not not_6 (not_6_out, Opcode[0]);
  not not_7 (not_7_out, Opcode[2]);
  not not_8 (not_8_out, Opcode[4]);
  and and_2 (Jump, not_6_out, not_5_out, not_7_out, not_8_out, not_4_out);
  not not_9 (not_9_out, Opcode[3]);
  not not_10 (not_10_out, Opcode[1]);
  not not_11 (not_11_out, Opcode[0]);
  not not_12 (not_12_out, Opcode[4]);
  and and_3 (beq, not_11_out, not_10_out, Opcode[2], not_12_out, not_14_out);
  not not_13 (not_13_out, Opcode[1]);
  not not_14 (not_14_out, Opcode[5]);
  not not_15 (not_15_out, Opcode[5]);
  not not_16 (not_16_out, Opcode[3]);
  not not_17 (not_17_out, Opcode[4]);
  and and_4 (bne, Opcode[0], not_13_out, Opcode[2], not_17_out, not_15_out);
  not not_18 (not_18_out, beq);
  not not_19 (not_19_out, Jump);
  not not_20 (not_20_out, bne);
  and and_5 (RegWrite, not_20_out, not_18_out, not_19_out);
  or or_1 (or_1_out, bne, beq);
  not not_21 (not_21_out, or_1_out);
  not not_22 (not_22_out, Jump);
  and and_6 (and_6_out, Opcode[3], Opcode[1]);
  and and_7 (ALUOp[1], not_21_out, not_22_out);
  or or_2 (ALUOp[1], and_6_out, or_1_out);

  assign ALUOp[0] = ALUOp[1];
endmodule

module _32_bit_ALU__DONE (
  input  Ainvert,
  input  Binvert,
  input  CarryIn,
  input  [1:0] Operation,
  input  [31:0] a,
  input  [31:0] b,
  input  [31:0] Less,
  input  [1:0] Shift_Operation,
  input  [4:0] Shamt,
  output Zero,
  output [31:0] Set,
  output CarryOut,
  output [31:0] Result
);

  wire or_2_out;
  wire [31:0] and_1_out, multiplexer_1_out, multiplexer_2_out, multiplexer_3_out, not_1_out, not_2_out,
       or_1_out, Shift_Left_out_3, Shift_Right_out_3;

  assign not_1_out = ~a;  // NOT_Gate not_1, 32 bits wide
  Multiplexer #(.width(32)) multiplexer_1 (
    .in0(a), .in1(not_1_out), .out(multiplexer_1_out), .sel(Ainvert));  // open: en
  assign not_2_out = ~b;  // NOT_Gate not_2, 32 bits wide
  Shift_Left__DONE Shift_Left (.Input(b), .Shamt(Shamt), .out_3(Shift_Left_out_3));
  Shift_Right__DONE Shift_Right (.Input(b), .Shamt(Shamt), .out_3(Shift_Right_out_3));
  Multiplexer #(.width(32)) multiplexer_2 (
    .in0(b), .in1(not_2_out), .out(multiplexer_2_out), .sel(Binvert));  // open: en
  assign and_1_out = multiplexer_1_out & multiplexer_2_out;  // AND_Gate and_1, 32 bits wide
  assign or_1_out = multiplexer_1_out | multiplexer_2_out;  // OR_Gate or_1, 32 bits wide
  Adder #(.width(32)) adder_1 (.a(multiplexer_1_out), .b(multiplexer_2_out), .out(Set), .cin(CarryIn), .cout(CarryOut));
  Multiplexer #(.select(2), .width(32)) multiplexer_3 (
    .in0(and_1_out), .in1(or_1_out), .in2(Set), .in3(Less), .out(multiplexer_3_out), .sel(Operation));  // open: en
  Multiplexer #(.select(2), .width(32)) multiplexer_4 (
    .in0(multiplexer_3_out), .in2(Shift_Left_out_3), .in3(Shift_Right_out_3), .out(Result),
    .sel(Shift_Operation));  // open: in1, en
  or or_2 (or_2_out, multiplexer_3_out[0], multiplexer_3_out[1], multiplexer_3_out[2], multiplexer_3_out[3], multiplexer_3_out[4], multiplexer_3_out[5], multiplexer_3_out[6], multiplexer_3_out[7], multiplexer_3_out[8], multiplexer_3_out[9], multiplexer_3_out[10], multiplexer_3_out[11], multiplexer_3_out[12], multiplexer_3_out[13], multiplexer_3_out[14], multiplexer_3_out[15], multiplexer_3_out[16], multiplexer_3_out[17], multiplexer_3_out[18], multiplexer_3_out[19], multiplexer_3_out[20], multiplexer_3_out[21], multiplexer_3_out[22], multiplexer_3_out[23], multiplexer_3_out[24], multiplexer_3_out[25], multiplexer_3_out[26], multiplexer_3_out[27], multiplexer_3_out[28], multiplexer_3_out[29], multiplexer_3_out[30], multiplexer_3_out[31]);
  not not_3 (Zero, or_2_out);
endmodule

module functControl__DONE (
  input  [5:0] funct,
  output [3:0] ALUControl,
  output [1:0] Shift_Control
);

  wire and_1_out, and_2_out, and_3_out, and_4_out, and_5_out, and_6_out, and_7_out, and_8_out, and_9_out,
       and_10_out, and_11_out, and_12_out, and_13_out, and_14_out, and_15_out, and_16_out, and_18_out,
       and_19_out, and_20_out, and_22_out, and_23_out, not_1_out, not_2_out, not_3_out, not_4_out, not_6_out,
       not_7_out, not_8_out;
  wire [1:0] and_21_out;

  not not_1 (not_1_out, funct[3]);
  not not_2 (not_2_out, funct[1]);
  not not_3 (not_3_out, funct[3]);
  not not_4 (not_4_out, funct[2]);
  not not_5 (ALUControl[1], funct[2]);
  not not_6 (not_6_out, funct[0]);
  not not_7 (not_7_out, funct[1]);
  not not_8 (not_8_out, funct[0]);
  and and_1 (and_1_out, not_1_out, funct[2]);
  and and_2 (and_2_out, funct[1], funct[0]);
  and and_3 (and_3_out, not_1_out, funct[2]);
  and and_4 (and_4_out, funct[1], funct[0]);
  and and_5 (and_5_out, funct[1], not_6_out);
  and and_6 (and_6_out, not_1_out, funct[2]);
  and and_7 (and_7_out, not_2_out, funct[0]);
  and and_8 (and_8_out, funct[3], ALUControl[1]);
  and and_9 (and_9_out, and_8_out, and_10_out);
  and and_10 (and_10_out, funct[1], not_6_out);
  and and_11 (and_11_out, not_3_out, not_4_out);
  and and_12 (and_12_out, funct[1], not_8_out);
  and and_13 (and_13_out, not_4_out, funct[1]);
  and and_14 (and_14_out, not_3_out, not_4_out);
  and and_15 (and_15_out, not_4_out, not_7_out);
  and and_16 (and_16_out, not_4_out, not_3_out);
  and and_17 (ALUControl[3], and_1_out, and_2_out);
  and and_18 (and_18_out, and_3_out, and_4_out);
  and and_19 (and_19_out, ALUControl[1], and_5_out);
  and and_20 (and_20_out, and_6_out, and_7_out);
  and and_21 (and_21_out[0], and_11_out, and_12_out);
  and and_22 (and_22_out, and_13_out, and_14_out);
  or or_1 (and_21_out[1], and_22_out, and_23_out);
  and and_23 (and_23_out, and_15_out, and_16_out);
  or or_2 (ALUControl[2], and_18_out, and_19_out);
  or or_3 (ALUControl[0], and_20_out, and_9_out);
  Multiplexer #(.width(2)) multiplexer_1 (
    .in0(and_21_out), .in1(2'b00), .out(Shift_Control), .sel(funct[5]));  // open: en
endmodule

module ALUControl__DONE (
  input  [5:0] funct,
  input  [1:0] ALUOp,
  output [3:0] ALUControl_output,
  output [1:0] Shift_Control
);

  wire [3:0] functcontrol_done_1_alucontrol;

  functControl__DONE functcontrol_done_1 (
    .funct(funct), .ALUControl(functcontrol_done_1_alucontrol), .Shift_Control(Shift_Control));
  Multiplexer #(.select(2), .width(4)) multiplexer_1 (
    .in0(4'b0010), .in1(4'b0110), .in2(functcontrol_done_1_alucontrol), .in3(functcontrol_done_1_alucontrol),
    .out(ALUControl_output), .sel(ALUOp));  // open: en
endmodule

module MIPS_CPU (
  input  [31:0] Write_Data_to__t9,
  input  Write_Signal_for__t9,
  output [31:0] From__t8,
  output [31:0] From__t9
);

  wire and_1_out, control_unit_done_1_beq, control_unit_done_1_jump, control_unit_done_1_regdst,
       control_unit_done_1_regwrite, n32_bit_alu_done_1_zero;
  wire [1:0] control_unit_done_1_aluop;
  wire [3:0] adder_1_out, alucontrol_done_1_alucontrol_output;
  wire [4:0] multiplexer_1_out;
  wire [27:0] adder_1_out_2;
  wire [31:0] adder_2_out, instruction_memory_done_1_out_2, multiplexer_2_out, multiplexer_3_out,
       multiplexer_4_out, multiplexer_5_out, n32_bit_alu_done_1_result, register_1_q,
       register_file_done_1_read_data_1, register_file_done_1_read_data_2, shifter_1_out,
       sign_extend_done_1_output;

  Register #(.width(32)) register_1 (.D(multiplexer_5_out), .Q(register_1_q));  // open: en, clk, clr
  Instruction_Memory__DONE instruction_memory_done_1 (
    .Address(register_1_q[17:2]), .out_2(instruction_memory_done_1_out_2));
  Adder #(.width(32)) adder_1 (.a(register_1_q), .b(32'h4), .out({adder_1_out, adder_1_out_2}));  // open: cin, cout
  Multiplexer #(.width(5)) multiplexer_1 (
    .in0(instruction_memory_done_1_out_2[20:16]), .in1(instruction_memory_done_1_out_2[15:11]),
    .out(multiplexer_1_out), .sel(control_unit_done_1_regdst));  // open: en
  Control_Unit__DONE control_unit_done_1 (
    .Opcode(instruction_memory_done_1_out_2[31:26]), .Jump(control_unit_done_1_jump),
    .beq(control_unit_done_1_beq), .RegWrite(control_unit_done_1_regwrite),
    .RegDst(control_unit_done_1_regdst), .ALUOp(control_unit_done_1_aluop));  // open: bne
  Register_File__DONE register_file_done_1 (
    .Read_Register_1(instruction_memory_done_1_out_2[25:21]), .RegWrite(control_unit_done_1_regwrite),
    .Write_Register(multiplexer_1_out), .Write_Data(multiplexer_4_out),
    .Read_Register_2(instruction_memory_done_1_out_2[20:16]), .Write_to__t9(Write_Data_to__t9),
    .Write_Signal(Write_Signal_for__t9), .Read_Data_1(register_file_done_1_read_data_1),
    .Read_Data_2(register_file_done_1_read_data_2), .t8_to_LCD(From__t8), .t9_to_Keypad(From__t9));  // open: Write_Enable, Clock
  Sign_Extend__DONE sign_extend_done_1 (
    .Input(instruction_memory_done_1_out_2[15:0]), .Output(sign_extend_done_1_output));
  Shifter #(.width(32)) shifter_1 (.in(sign_extend_done_1_output), .\dist (5'b00010), .out(shifter_1_out));
  Multiplexer #(.width(32)) multiplexer_2 (
    .in0(register_file_done_1_read_data_2), .in1(sign_extend_done_1_output), .out(multiplexer_2_out));  // open: sel, en
  ALUControl__DONE alucontrol_done_1 (
    .funct(instruction_memory_done_1_out_2[5:0]), .ALUOp(control_unit_done_1_aluop),
    .ALUControl_output(alucontrol_done_1_alucontrol_output));  // open: Shift_Control
  Adder #(.width(32)) adder_2 (
    .a({adder_1_out, adder_1_out_2}), .b(shifter_1_out), .out(adder_2_out));  // open: cin, cout
  and and_1 (and_1_out, control_unit_done_1_beq, n32_bit_alu_done_1_zero);
  _32_bit_ALU__DONE u_32_bit_alu_done_1 (
    .a(register_file_done_1_read_data_1), .b(multiplexer_2_out),
    .Ainvert(alucontrol_done_1_alucontrol_output[3]), .Binvert(alucontrol_done_1_alucontrol_output[2]),
    .Operation(alucontrol_done_1_alucontrol_output[1:0]), .Zero(n32_bit_alu_done_1_zero),
    .Result(n32_bit_alu_done_1_result));  // open: Less, Shamt, CarryIn, CarryOut, Shift_Operation, Set
  Multiplexer #(.width(32)) multiplexer_3 (
    .in0({adder_1_out, adder_1_out_2}), .in1(adder_2_out), .out(multiplexer_3_out), .sel(and_1_out));  // open: en
  Multiplexer #(.width(32)) multiplexer_4 (
    .in0(n32_bit_alu_done_1_result), .in1(n32_bit_alu_done_1_result), .out(multiplexer_4_out));  // open: sel, en
  Multiplexer #(.width(32)) multiplexer_5 (
    .in0({adder_1_out, instruction_memory_done_1_out_2[25:0], 2'b00}), .in1(multiplexer_3_out),
    .out(multiplexer_5_out), .sel(control_unit_done_1_jump));  // open: en
endmodule
